// Logisim project CSC3410-MicroArchitecture.circ as structural Verilog: 11 circuits, main circuit main
module main (
);

  wire clock_1_out, decoder_1_out0, decoder_1_out1, decoder_1_out2, decoder_1_out3, decoder_1_out4,
       decoder_1_out5, decoder_1_out6, decoder_1_out7, decoder_1_out8, n32bitalu_1_n_flag,
       n32bitalu_1_z_flag, undriven, undriven_2, undriven_3, undriven_4, undriven_6, undriven_7, undriven_8,
       undriven_9, undriven_10, undriven_12;
  wire [1:0] undriven_11;
  wire [5:0] undriven_5;
  wire [31:0] b_bus_1_out_10, mbr_1_out_5, mbr_1_out_6, n32bitalu_1_out_5, n32bitmemlocation_2_out_5,
       n32bitmemlocation_3_out_5, n32bitmemlocation_4_out_5, n32bitmemlocation_5_out_5,
       n32bitmemlocation_6_out_5, n32bitmemlocation_7_out_5, n32bitmemlocation_8_out_5,
       n32bitmemlocation_9_out_5, shifter_1_out_3;

  Clock clock_1 (.out(clock_1_out));
  _32BitMemLocation u_32bitmemlocation_1 (
    .in_1(shifter_1_out_3), .Enabled(undriven_6), .Clock(clock_1_out));  // open: Enable_Output, out_5
  _32BitMemLocation u_32bitmemlocation_2 (
    .in_1(shifter_1_out_3), .Enabled(undriven), .Enable_Output(decoder_1_out0),
    .out_5(n32bitmemlocation_2_out_5), .Clock(clock_1_out));
  _32BitMemLocation u_32bitmemlocation_3 (
    .in_1(shifter_1_out_3), .Enabled(undriven_7), .Enable_Output(decoder_1_out1),
    .out_5(n32bitmemlocation_3_out_5), .Clock(clock_1_out));
  MBR mbr_1 (
    .Clock(clock_1_out), .Signed(decoder_1_out2), .Unsigned(decoder_1_out3), .out_5(mbr_1_out_5),
    .out_6(mbr_1_out_6));  // open: Input
  _32BitMemLocation u_32bitmemlocation_4 (
    .in_1(shifter_1_out_3), .Enabled(undriven_8), .Enable_Output(decoder_1_out4),
    .out_5(n32bitmemlocation_4_out_5), .Clock(clock_1_out));
  _32BitMemLocation u_32bitmemlocation_5 (
    .in_1(shifter_1_out_3), .Enabled(undriven_2), .Enable_Output(decoder_1_out5),
    .out_5(n32bitmemlocation_5_out_5), .Clock(clock_1_out));
  _32BitMemLocation u_32bitmemlocation_6 (
    .in_1(shifter_1_out_3), .Enabled(undriven_3), .Enable_Output(decoder_1_out6),
    .out_5(n32bitmemlocation_6_out_5), .Clock(clock_1_out));
  _32BitMemLocation u_32bitmemlocation_7 (
    .in_1(shifter_1_out_3), .Enabled(undriven_4), .Enable_Output(decoder_1_out7),
    .out_5(n32bitmemlocation_7_out_5), .Clock(clock_1_out));
  _32BitMemLocation u_32bitmemlocation_8 (
    .in_1(shifter_1_out_3), .Enabled(undriven_9), .Enable_Output(decoder_1_out8),
    .out_5(n32bitmemlocation_8_out_5), .Clock(clock_1_out));
  _32BitMemLocation u_32bitmemlocation_9 (
    .in_1(shifter_1_out_3), .Enabled(undriven_10), .out_5(n32bitmemlocation_9_out_5), .Clock(clock_1_out));  // open: Enable_Output
  B_Bus b_bus_1 (
    .in_1(n32bitmemlocation_2_out_5), .in_2(n32bitmemlocation_3_out_5), .in_3(mbr_1_out_5),
    .in_4(mbr_1_out_6), .in_5(n32bitmemlocation_4_out_5), .in_6(n32bitmemlocation_5_out_5),
    .in_7(n32bitmemlocation_6_out_5), .in_8(n32bitmemlocation_7_out_5), .in_9(n32bitmemlocation_8_out_5),
    .out_10(b_bus_1_out_10));
  _32BitALU u_32bitalu_1 (
    .in_1(n32bitmemlocation_9_out_5), .in_2(b_bus_1_out_10), .in_3(undriven_5), .Z_Flag(n32bitalu_1_z_flag),
    .out_5(n32bitalu_1_out_5), .N_Flag(n32bitalu_1_n_flag));  // open: Carry_Out
  Shifter shifter_1 (.in_1(n32bitalu_1_out_5), .Controls(undriven_11), .out_3(shifter_1_out_3));
  Decoder #(.select(4)) decoder_1 (
    .out0(decoder_1_out0), .out1(decoder_1_out1), .out2(decoder_1_out2), .out3(decoder_1_out3),
    .out4(decoder_1_out4), .out5(decoder_1_out5), .out6(decoder_1_out6), .out7(decoder_1_out7),
    .out8(decoder_1_out8), .en(undriven_12));  // open: out9, out10, out11, out12, out13, out14, out15, sel

  // Notes on the sheet:
  //   Nick Zayatz
  //   Michele Burns
  //   Michael Newton
  //   Charlie Adams
  //   10/20/15
  //   Main File for CSC3410-MicroArchitecture Project
endmodule

module _1BitAdder (
  input  Carry_In,
  input  A,
  input  B,
  input  Function,
  output Result,
  output Carry_Out
);

  wire and_1_out, and_2_out, xor_1_out, xor_2_out;

  and and_1 (and_1_out, Function, B, A);
  or or_1 (Carry_Out, and_1_out, and_2_out);
  xor xor_1 (xor_1_out, A, B);
  and and_2 (and_2_out, Function, xor_1_out, Carry_In);
  xor xor_2 (xor_2_out, Carry_In, xor_1_out);
  and and_3 (Result, xor_2_out, Function);
endmodule

module _1BitALU (
  input  Carry_In,
  input  A,
  input  ENA,
  input  B,
  input  ENB,
  input  in_6,
  input  F1,
  input  F0,
  output Output,
  output out_10
);

  wire and_1_out, and_2_out, and_3_out, and_4_out, and_5_out, and_6_out, decoder_1_out0, decoder_1_out1,
       decoder_1_out2, decoder_1_out3, n1bitadder_1_result, not_1_out, or_1_out, xor_1_out;

  and and_1 (and_1_out, ENA, B);
  and and_2 (and_2_out, ENB, in_6);
  xor xor_1 (xor_1_out, A, and_1_out);
  not not_1 (not_1_out, and_2_out);
  Decoder #(.select(2)) decoder_1 (
    .out0(decoder_1_out0), .out1(decoder_1_out1), .out2(decoder_1_out2), .out3(decoder_1_out3), .sel({F0, F1}));  // open: en
  and and_3 (and_3_out, xor_1_out, and_2_out);
  or or_1 (or_1_out, xor_1_out, and_2_out);
  and and_4 (and_4_out, and_3_out, decoder_1_out0);
  and and_5 (and_5_out, or_1_out, decoder_1_out1);
  and and_6 (and_6_out, not_1_out, decoder_1_out2);
  _1BitAdder u_1bitadder_1 (
    .A(and_2_out), .B(xor_1_out), .Function(decoder_1_out3), .Result(n1bitadder_1_result),
    .Carry_In(Carry_In), .Carry_Out(out_10));
  or or_2 (Output, and_4_out, and_5_out, and_6_out, n1bitadder_1_result);

  // Notes on the sheet:
  //   INVA
endmodule

module _8BitALU (
  input  F1,
  input  F0,
  input  ENB,
  input  [7:0] B,
  input  ENA,
  input  [7:0] A,
  input  INVA,
  input  in_8,
  output [7:0] out_9,
  output Carry_Out
);

  wire n1bitalu_2_out_10, n1bitalu_3_out_10, n1bitalu_4_out_10, n1bitalu_5_out_10, n1bitalu_6_out_10,
       n1bitalu_7_out_10, n1bitalu_8_out_10;

  _1BitALU u_1bitalu_1 (
    .Carry_In(n1bitalu_2_out_10), .A(INVA), .ENA(A[7]), .B(ENA), .ENB(B[7]), .in_6(ENB), .F1(F1), .F0(F0),
    .Output(out_9[7]), .out_10(Carry_Out));
  _1BitALU u_1bitalu_2 (
    .Carry_In(n1bitalu_3_out_10), .A(INVA), .ENA(A[6]), .B(ENA), .ENB(B[6]), .in_6(ENB), .F1(F1), .F0(F0),
    .Output(out_9[6]), .out_10(n1bitalu_2_out_10));
  _1BitALU u_1bitalu_3 (
    .Carry_In(n1bitalu_4_out_10), .A(INVA), .ENA(A[5]), .B(ENA), .ENB(B[5]), .in_6(ENB), .F1(F1), .F0(F0),
    .Output(out_9[5]), .out_10(n1bitalu_3_out_10));
  _1BitALU u_1bitalu_4 (
    .Carry_In(n1bitalu_5_out_10), .A(INVA), .ENA(A[4]), .B(ENA), .ENB(B[4]), .in_6(ENB), .F1(F1), .F0(F0),
    .Output(out_9[4]), .out_10(n1bitalu_4_out_10));
  _1BitALU u_1bitalu_5 (
    .Carry_In(n1bitalu_6_out_10), .A(INVA), .ENA(A[3]), .B(ENA), .ENB(B[3]), .in_6(ENB), .F1(F1), .F0(F0),
    .Output(out_9[3]), .out_10(n1bitalu_5_out_10));
  _1BitALU u_1bitalu_6 (
    .Carry_In(n1bitalu_7_out_10), .A(INVA), .ENA(A[2]), .B(ENA), .ENB(B[2]), .in_6(ENB), .F1(F1), .F0(F0),
    .Output(out_9[2]), .out_10(n1bitalu_6_out_10));
  _1BitALU u_1bitalu_7 (
    .Carry_In(n1bitalu_8_out_10), .A(INVA), .ENA(A[1]), .B(ENA), .ENB(B[1]), .in_6(ENB), .F1(F1), .F0(F0),
    .Output(out_9[1]), .out_10(n1bitalu_7_out_10));
  _1BitALU u_1bitalu_8 (
    .Carry_In(in_8), .A(INVA), .ENA(A[0]), .B(ENA), .ENB(B[0]), .in_6(ENB), .F1(F1), .F0(F0),
    .Output(out_9[0]), .out_10(n1bitalu_8_out_10));

  // Notes on the sheet:
  //   Out
  //   Carry In
endmodule

module _32BitALU (
  input  [31:0] in_1,
  input  [31:0] in_2,
  input  [5:0] in_3,
  output Z_Flag,
  output [31:0] out_5,
  output N_Flag,
  output Carry_Out
);

  wire n8bitalu_1_carry_out, n8bitalu_2_carry_out, n8bitalu_3_carry_out;

  _8BitALU u_8bitalu_1 (
    .out_9(out_5[7:0]), .F1(in_3[4]), .F0(in_3[5]), .ENB(in_3[2]), .B(in_2[7:0]), .ENA(in_3[3]),
    .A(in_1[7:0]), .INVA(in_3[1]), .in_8(in_3[0]), .Carry_Out(n8bitalu_1_carry_out));
  _8BitALU u_8bitalu_2 (
    .out_9(out_5[15:8]), .F1(in_3[4]), .F0(in_3[5]), .ENB(in_3[2]), .B(in_2[15:8]), .ENA(in_3[3]),
    .A(in_1[15:8]), .INVA(in_3[1]), .in_8(n8bitalu_1_carry_out), .Carry_Out(n8bitalu_2_carry_out));
  _8BitALU u_8bitalu_3 (
    .out_9(out_5[23:16]), .F1(in_3[4]), .F0(in_3[5]), .ENB(in_3[2]), .B(in_2[23:16]), .ENA(in_3[3]),
    .A(in_1[23:16]), .INVA(in_3[1]), .in_8(n8bitalu_2_carry_out), .Carry_Out(n8bitalu_3_carry_out));
  _8BitALU u_8bitalu_4 (
    .out_9({N_Flag, out_5[30:24]}), .F1(in_3[4]), .F0(in_3[5]), .ENB(in_3[2]), .B(in_2[31:24]),
    .ENA(in_3[3]), .A(in_1[31:24]), .INVA(in_3[1]), .in_8(n8bitalu_3_carry_out), .Carry_Out(Carry_Out));
  nor nor_1 (Z_Flag, out_5[0], out_5[1], out_5[2], out_5[3], out_5[4], out_5[5], out_5[6], out_5[7], out_5[8], out_5[9], out_5[10], out_5[11], out_5[12], out_5[13], out_5[14], out_5[15], out_5[16], out_5[17], out_5[18], out_5[19], out_5[20], out_5[21], out_5[22], out_5[23], out_5[24], out_5[25], out_5[26], out_5[27], out_5[28], out_5[29], out_5[30], N_Flag);

  assign out_5[31] = N_Flag;

  // Notes on the sheet:
  //   Carry In
  //   INVA
  //   A
  //   ENA
  //   B
  //   ENB
  //   F0
  //   F1
  //   Output
endmodule

module Shifter (
  input  [31:0] in_1,
  input  [1:0] Controls,
  output [31:0] out_3
);

  wire [31:0] demultiplexer_1_out0, demultiplexer_1_out1, demultiplexer_1_out2, demultiplexer_1_out3,
       shifter_1_out, shifter_2_out, undriven;

  Demultiplexer #(.select(2), .width(32)) demultiplexer_1 (
    .out0(demultiplexer_1_out0), .out1(demultiplexer_1_out1), .out2(demultiplexer_1_out2),
    .out3(demultiplexer_1_out3), .in(in_1), .sel(Controls));  // open: en
  Shifter_part #(.width(32), .shift("ar")) shifter_1 (
    .in(demultiplexer_1_out1), .\dist (5'b00001), .out(shifter_1_out));
  Shifter_part #(.width(32)) shifter_2 (.in(demultiplexer_1_out2), .\dist (5'b01000), .out(shifter_2_out));
  Multiplexer #(.select(2), .width(32)) multiplexer_1 (
    .in0(demultiplexer_1_out0), .in1(shifter_1_out), .in2(shifter_2_out), .in3(undriven), .out(out_3),
    .sel(Controls));  // open: en

  // Notes on the sheet:
  //   Input
  //   Shifter
  //   Output
endmodule

module _1BitMemLocation (
  input  Clock,
  input  in_2,
  input  Enabled,
  output out_4
);

  wire not_1_out;

  not not_1 (not_1_out, Clock);
  J_K_Flip_Flop j_k_ff_1 (.J(Clock), .clk(in_2), .K(not_1_out), .Q(out_4), .en(Enabled));  // open: Qn, preset, reset

  // Notes on the sheet:
  //   Input
endmodule

module _8BitMemLocation (
  input  [7:0] in_1,
  input  Clock,
  input  Enabled,
  output [7:0] Memory
);

  _1BitMemLocation u_1bitmemlocation_1 (.Clock(in_1[7]), .in_2(Clock), .Enabled(Enabled), .out_4(Memory[7]));
  _1BitMemLocation u_1bitmemlocation_2 (.Clock(in_1[6]), .in_2(Clock), .Enabled(Enabled), .out_4(Memory[6]));
  _1BitMemLocation u_1bitmemlocation_3 (.Clock(in_1[5]), .in_2(Clock), .Enabled(Enabled), .out_4(Memory[5]));
  _1BitMemLocation u_1bitmemlocation_4 (.Clock(in_1[4]), .in_2(Clock), .Enabled(Enabled), .out_4(Memory[4]));
  _1BitMemLocation u_1bitmemlocation_5 (.Clock(in_1[3]), .in_2(Clock), .Enabled(Enabled), .out_4(Memory[3]));
  _1BitMemLocation u_1bitmemlocation_6 (.Clock(in_1[2]), .in_2(Clock), .Enabled(Enabled), .out_4(Memory[2]));
  _1BitMemLocation u_1bitmemlocation_7 (.Clock(in_1[1]), .in_2(Clock), .Enabled(Enabled), .out_4(Memory[1]));
  _1BitMemLocation u_1bitmemlocation_8 (.Clock(in_1[0]), .in_2(Clock), .Enabled(Enabled), .out_4(Memory[0]));

  // Notes on the sheet:
  //   Input
endmodule

module _32BitMemLocation (
  input  [31:0] in_1,
  input  Clock,
  input  Enabled,
  input  Enable_Output,
  output [31:0] out_5
);

  wire [7:0] n8bitmemlocation_1_memory, n8bitmemlocation_2_memory, n8bitmemlocation_3_memory,
       n8bitmemlocation_4_memory;
  wire [31:0] bit_extender_1_out;

  _8BitMemLocation u_8bitmemlocation_1 (
    .in_1(in_1[31:24]), .Clock(Clock), .Enabled(Enabled), .Memory(n8bitmemlocation_1_memory));
  _8BitMemLocation u_8bitmemlocation_2 (
    .in_1(in_1[23:16]), .Clock(Clock), .Enabled(Enabled), .Memory(n8bitmemlocation_2_memory));
  _8BitMemLocation u_8bitmemlocation_3 (
    .in_1(in_1[15:8]), .Clock(Clock), .Enabled(Enabled), .Memory(n8bitmemlocation_3_memory));
  _8BitMemLocation u_8bitmemlocation_4 (
    .in_1(in_1[7:0]), .Clock(Clock), .Enabled(Enabled), .Memory(n8bitmemlocation_4_memory));
  assign bit_extender_1_out = {{31{Enable_Output}}, Enable_Output};  // Bit_Extender bit_extender_1
  assign out_5 = {n8bitmemlocation_1_memory, n8bitmemlocation_2_memory, n8bitmemlocation_3_memory, n8bitmemlocation_4_memory} & bit_extender_1_out;  // AND_Gate and_1, 32 bits wide

  // Notes on the sheet:
  //   Input
  //   Output
endmodule

module B_Bus (
  input  [31:0] in_1,
  input  [31:0] in_2,
  input  [31:0] in_3,
  input  [31:0] in_4,
  input  [31:0] in_5,
  input  [31:0] in_6,
  input  [31:0] in_7,
  input  [31:0] in_8,
  input  [31:0] in_9,
  output [31:0] out_10
);

  assign out_10 = in_9 | in_8 | in_7 | in_6 | in_5 | in_4 | in_3 | in_2 | in_1;  // OR_Gate or_1, 32 bits wide
endmodule

module MBR (
  input  [7:0] Input,
  input  Clock,
  input  Signed,
  input  Unsigned,
  output [31:0] out_5,
  output [31:0] out_6
);

  wire [7:0] n8bitmemlocation_1_memory;
  wire [31:0] bit_extender_1_out, bit_extender_2_out, bit_extender_3_out, bit_extender_4_out;

  _8BitMemLocation u_8bitmemlocation_1 (
    .in_1(Input), .Clock(Clock), .Enabled(1'b1), .Memory(n8bitmemlocation_1_memory));
  assign bit_extender_1_out = {{31{Signed}}, Signed};  // Bit_Extender bit_extender_1
  assign bit_extender_2_out = {{24{n8bitmemlocation_1_memory[7]}}, n8bitmemlocation_1_memory};  // Bit_Extender bit_extender_2
  assign bit_extender_3_out = {{24{1'b0}}, n8bitmemlocation_1_memory};  // Bit_Extender bit_extender_3
  assign bit_extender_4_out = {{31{Unsigned}}, Unsigned};  // Bit_Extender bit_extender_4
  assign out_5 = bit_extender_1_out & bit_extender_2_out;  // AND_Gate and_1, 32 bits wide
  assign out_6 = bit_extender_3_out & bit_extender_4_out;  // AND_Gate and_2, 32 bits wide

  // Notes on the sheet:
  //   Signed Output
  //   Unsigned Output
endmodule
